# Fritzing sketch SmartRfSwitch (saved by Fritzing 1.0.4)
circuit board: 5cm x 4cm
breadboards: 1

parts:
  R1 = Resistor [tolerance=±5% power=0.25W resistance=1k package=THT]
  Q1 = NPN-Transistor [mn=2N3904 package="TO92 [THT]"]
  R2 = Resistor [tolerance=±5% power=0.25W resistance=1k package=THT]
  R3 = Resistor [tolerance=±5% power=0.25W resistance=10k package=THT]
  J1_2 = male pin header, 2 pins [form="♂ (male)"]
  J1_1 = male pin header, 2 pins [form="♂ (male)"]
  U1 = Sharp PC817 [mn=NEC2561 package=THT]
  R4 = Resistor [tolerance=±5% power=0.25W resistance=150 package=THT]
  R5 = Resistor [tolerance=±5% power=0.25W resistance=1k package=THT]
  R6 = Resistor [tolerance=±5% power=0.25W resistance=10k package=THT]
  J2 = male pin header, 3 pins [form="♂ (male)"]
  U2 = Sharp PC817 [mn=NEC2561 package=THT]
  R7 = Resistor [tolerance=±5% power=0.25W resistance=330 package=THT]
  R8 = Resistor [tolerance=±5% power=0.25W resistance=10k package=THT]
  R9 = Resistor [tolerance=±5% power=0.25W resistance=1k package=THT]
  J3_1 = female pin header, 8 pins [form="♀ (female)"]
  J3_2 = female pin header, 8 pins [form="♀ (female)"]
  Q2 = NPN-Transistor [mn=2N3904 package="TO92 [THT]"]
  J3 = Screw terminal - 2 pins [package=THT]

nets:
  GPIO8: R1.Pin_0, J3_1.pin5
  N1: R1.Pin_1, Q1.B
  GND: Q1.E, J1_1.pin2, U1.Pin_2, R6.Pin_1, J2.pin3, U2.Pin_2, R8.Pin_1, J3_2.pin7, Q2.E, J3.pin1
  N2: Q1.C, R2.Pin_0, R3.Pin_1
  N3: R2.Pin_1, Q2.B
  5V: R3.Pin_0, J1_2.pin1, U1.Pin_4, J3_2.pin8, J3.pin2
  N4: J1_2.pin2, Q2.C
  GPIO9: J1_1.pin1, J3_1.pin4
  N5: U1.Pin_1, R4.Pin_1
  N6: U1.Pin_3, R5.Pin_0, R6.Pin_0
  GPIO3: R4.Pin_0, J3_2.pin4
  N7: R5.Pin_1, J2.pin2
  N8: J2.pin1, R7.Pin_1
  N9: U2.Pin_1, R7.Pin_0
  3.3V: U2.Pin_4, J3_2.pin6
  N10: U2.Pin_3, R8.Pin_0, R9.Pin_1
  GPIO10: R9.Pin_0, J3_1.pin3
  GPIO21: J3_1.pin1
  GPIO20: J3_1.pin2
  GPIO7: J3_1.pin6
  GPIO6: J3_1.pin7
  GPIO5: J3_1.pin8
  GPIO0: J3_2.pin1
  GPIO1: J3_2.pin2
  GPIO2: J3_2.pin3
  GPIO4: J3_2.pin5
